# Fritzing sketch XY-MK-5V (saved by Fritzing 0.9.0b)
breadboards: 1

parts:
  Part1 = SRF05 Ultrasonic Rangefinder
  Part2 = Arduino Nano (Rev3.0)

nets:
  VCC: Part1.VCC, Part2.5V
  N1: Part1.Trig, Part2.D8
  N2: Part1.Echo, Part2.D9
  GND: Part1.GND, Part2.GND
